# Fritzing sketch plotter_circuit (saved by Fritzing 0.9.3b)

parts:
  Composant1 = Arduino Uno (Rev3)
  M2 = Dagu DGServo 9g (Top view) [part_number=RS001B]
  Driver2 = 28BYJ-48 Driver Module [part_number=ULN2003 package=THT]
  X1 = USB Connectors [package=usb-minib-old]
  MOTOR1 = 28BYJ-48 Stepper Motor
  MOTOR2 = 28BYJ-48 Stepper Motor
  Driver3 = 28BYJ-48 Driver Module [part_number=ULN2003 package=THT]

nets:
  N1: Composant1.D8, Driver2.IN4
  N2: Composant1.D9_PWM, Driver2.IN3
  N3: Composant1.D10_PWM/SS, Driver2.IN2
  N4: Composant1.D11_PWM/MOSI, Driver2.IN1
  N5: Composant1.D2, Driver3.IN4
  N6: Composant1.D3_PWM, Driver3.IN3
  N7: Composant1.D4, Driver3.IN2
  N8: Composant1.D5_PWM, Driver3.IN1
  N9: Composant1.D6_PWM, M2.pulse
  N10: M2.gnd, X1.VBUS
  N11: M2.vcc, X1.D-
  N12: Driver2.blue-pin, MOTOR1.BLUE
  N13: Driver2.pink-pin, MOTOR1.PINK
  N14: Driver2.yellow-pin, MOTOR1.YELLOW
  N15: Driver2.orange-pin, MOTOR1.ORANGE
  N16: Driver2.red-pin, MOTOR1.RED
  N17: MOTOR2.RED, Driver3.red-pin
  N18: MOTOR2.ORANGE, Driver3.orange-pin
  N19: MOTOR2.YELLOW, Driver3.yellow-pin
  N20: MOTOR2.PINK, Driver3.pink-pin
  N21: MOTOR2.BLUE, Driver3.blue-pin

custom parts:
  28BYJ-48 Driver Module: Generic male header
